// Logisim project xz.circ as structural Verilog
module main (
  input  [3:0] A,
  input  [3:0] B,
  output out_3,
  output out_4,
  output out_5,
  output out_6,
  output out_7,
  output out_8,
  output out_9,
  output out_10
);

  wire [4:0] adder_1_out, adder_2_out, bit_extender_1_out, bit_extender_2_out;

  assign bit_extender_1_out = {{1{1'b0}}, A};  // Bit_Extender bit_extender_1
  assign bit_extender_2_out = {{1{1'b0}}, B};  // Bit_Extender bit_extender_2
  Adder #(.width(5)) adder_1 (
    .a(bit_extender_1_out), .b(bit_extender_2_out), .out(adder_1_out), .cin(1'b0));  // open: cout
  Adder #(.width(5)) adder_2 (.a(adder_1_out), .b(5'b01001), .out(adder_2_out), .cin(1'b0));  // open: cout
  bcd22 bcd22_1 (
    .S4(adder_2_out[4]), .S3(adder_2_out[3]), .S2(adder_2_out[2]), .S1(adder_2_out[1]), .S0(adder_2_out[0]),
    .T1(out_5), .T0(out_6), .U3(out_7), .U2(out_8), .U1(out_9), .U0(out_10));

  assign out_3 = 1'b0;
  assign out_4 = 1'b0;
endmodule

module Enc_8421 (
  input  S4,
  input  S3,
  input  S2,
  input  S1,
  input  S0,
  output T1,
  output T0,
  output U3,
  output U2,
  output U1,
  output U0
);

  wire and_1_out, and_2_out, and_3_out, and_4_out, and_5_out, and_6_out, and_7_out, and_8_out, and_9_out,
       and_10_out, and_11_out, and_12_out, and_13_out, and_14_out, and_15_out, and_16_out, and_17_out,
       and_18_out, and_19_out, and_20_out, and_21_out, and_22_out, not_1_out, not_2_out, not_3_out, not_4_out;

  not not_1 (not_1_out, S4);
  not not_2 (not_2_out, S3);
  not not_3 (not_3_out, S2);
  not not_4 (not_4_out, S1);
  not not_5 (U0, S0);
  and and_1 (and_1_out, S4, not_2_out, not_3_out, not_4_out);
  and and_2 (and_2_out, S4, not_2_out, not_3_out, U0);
  and and_3 (and_3_out, not_1_out, S3, S1, S0);
  and and_4 (and_4_out, not_1_out, S3, S2);
  and and_5 (and_5_out, not_2_out, S2);
  and and_6 (and_6_out, not_1_out, not_2_out, S0);
  and and_7 (and_7_out, S3, not_3_out, not_4_out);
  and and_8 (and_8_out, not_1_out, not_3_out, S1, U0);
  and and_9 (and_9_out, not_1_out, not_2_out, not_3_out, not_4_out, U0);
  and and_10 (and_10_out, S3, not_3_out, not_4_out, S0);
  and and_11 (and_11_out, S3, not_3_out, S1, U0);
  and and_12 (and_12_out, not_2_out, S2, S0);
  and and_13 (and_13_out, not_2_out, S2, S1);
  and and_14 (and_14_out, S3, not_3_out, not_4_out, U0);
  and and_15 (and_15_out, S2, S1, S0);
  and and_16 (and_16_out, S4, S0);
  and and_17 (and_17_out, S4, S1);
  and and_18 (and_18_out, not_2_out, S1, S0);
  and and_19 (and_19_out, not_2_out, S2, not_4_out, U0);
  and and_20 (and_20_out, S3, not_3_out, not_4_out, U0);
  and and_21 (and_21_out, S3, S2, not_4_out, S0);
  and and_22 (and_22_out, S3, S2, S1, U0);
  or or_1 (T1, and_1_out, and_2_out, and_3_out, and_4_out);
  or or_2 (T0, and_5_out, and_6_out, and_7_out, and_8_out);
  or or_3 (U3, and_9_out, and_10_out, and_11_out);
  or or_4 (U2, S4, and_12_out, and_13_out, and_14_out, and_15_out);
  or or_5 (U1, and_16_out, and_17_out, and_18_out, and_19_out, and_20_out, and_21_out, and_22_out);
endmodule

module Enc_84212 (
  input  S4,
  input  S3,
  input  S2,
  input  S1,
  input  S0,
  output T1,
  output T0,
  output U3,
  output U2,
  output U1,
  output U0
);

  wire and_1_out, and_2_out, and_3_out, and_4_out, and_5_out, and_6_out, and_7_out, and_8_out, and_9_out,
       and_10_out, and_11_out, and_12_out, and_13_out, and_14_out, and_15_out, and_16_out, and_17_out,
       and_18_out, and_19_out, and_20_out, and_21_out, and_22_out, not_1_out, not_2_out, not_3_out, not_4_out;

  not not_1 (not_1_out, S4);
  not not_2 (not_2_out, S3);
  not not_3 (not_3_out, S2);
  not not_4 (not_4_out, S1);
  not not_5 (U0, S0);
  and and_1 (and_1_out, S4, not_2_out, not_3_out, not_4_out);
  and and_2 (and_2_out, S4, not_2_out, not_3_out, U0);
  and and_3 (and_3_out, not_1_out, S3, S1, S0);
  and and_4 (and_4_out, not_1_out, S3, S2);
  and and_5 (and_5_out, not_2_out, S2);
  and and_6 (and_6_out, not_1_out, not_2_out, S0);
  and and_7 (and_7_out, S3, not_3_out, not_4_out);
  and and_8 (and_8_out, not_1_out, not_3_out, S1, U0);
  and and_9 (and_9_out, not_1_out, not_2_out, not_3_out, not_4_out, U0);
  and and_10 (and_10_out, S3, not_3_out, not_4_out, S0);
  and and_11 (and_11_out, S3, not_3_out, S1, U0);
  and and_12 (and_12_out, not_2_out, S2, S0);
  and and_13 (and_13_out, not_2_out, S2, S1);
  and and_14 (and_14_out, S3, not_3_out, not_4_out, U0);
  and and_15 (and_15_out, S2, S1, S0);
  and and_16 (and_16_out, S4, S0);
  and and_17 (and_17_out, S4, S1);
  and and_18 (and_18_out, not_2_out, S1, S0);
  and and_19 (and_19_out, not_2_out, S2, not_4_out, U0);
  and and_20 (and_20_out, S3, not_3_out, not_4_out, U0);
  and and_21 (and_21_out, S3, S2, not_4_out, S0);
  and and_22 (and_22_out, S3, S2, S1, U0);
  or or_1 (T1, and_1_out, and_2_out, and_3_out, and_4_out);
  or or_2 (T0, and_5_out, and_6_out, and_7_out, and_8_out);
  or or_3 (U3, and_9_out, and_10_out, and_11_out);
  or or_4 (U2, S4, and_12_out, and_13_out, and_14_out, and_15_out);
  or or_5 (U1, and_16_out, and_17_out, and_18_out, and_19_out, and_20_out, and_21_out, and_22_out);
endmodule

module bcd22 (
  input  S4,
  input  S3,
  input  S2,
  input  S1,
  input  S0,
  output T1,
  output T0,
  output U3,
  output U2,
  output U1,
  output U0
);

  wire and_1_out, and_2_out, and_3_out, and_4_out, and_5_out, and_6_out, and_7_out, and_8_out, not_1_out,
       not_2_out, not_3_out;

  not not_1 (not_1_out, S3);
  not not_2 (not_2_out, S2);
  not not_3 (not_3_out, S1);
  not not_4 (U0, S0);
  or or_1 (T0, S0, S1, S2, S3);
  and and_1 (and_1_out, not_1_out, not_2_out, not_3_out, U0);
  and and_2 (and_2_out, S3, S0);
  and and_3 (and_3_out, S2, S0);
  and and_4 (and_4_out, S2, S1);
  and and_5 (and_5_out, S3, U0);
  and and_6 (and_6_out, S1, S0);
  and and_7 (and_7_out, S2, not_3_out, U0);
  and and_8 (and_8_out, S3, U0);
  or or_2 (U3, and_1_out, and_2_out);
  or or_3 (U2, and_3_out, and_4_out, and_5_out);
  or or_4 (U1, and_6_out, and_7_out, and_8_out);

  assign T1 = 1'b0;
endmodule
